// Logisim project rv32i_processor_logisim_implementation.circ as structural Verilog: 13 circuits, main circuit main
module main (
);

  wire byteEnable0, byteEnable1, byteEnable2, byteEnable3, clk, comparator_1_eq, comparator_2_eq,
       comparator_3_eq, comparator_4_eq, comparator_5_eq, comparator_6_eq, comparator_7_eq, comparator_8_eq,
       comparator_9_eq, comparator_10_eq, or_1_out;
  wire [1:0] byteSel;
  wire [2:0] funct3_t;
  wire [3:0] multiplexer_2_out, multiplexer_3_out;
  wire [4:0] multiplexer_5_out, opcode5_t, rd_t, rs1_t, rs2_t;
  wire [6:0] funct7_t;
  wire [31:0] adder_1_out, adder_2_out, adder_4_out, ALU_res, bit_extender_1_out, bit_extender_2_out,
       bit_extender_3_out, bit_extender_4_out, branchhandler_1_branchpc, currPC, imm_t, inPC_t, ins_t,
       multiplexer_6_out, myRAM_dout, PCplus4, RAM_res, rd_val_t, register_1_q, rs1_val_t, rs2_val_t,
       shifter_1_out;
  wire [31:2] adder_3_out;

  Clock clock_1 (.out(clk));
  branchHandler branchhandler_1 (
    .currPC(currPC), .imm(imm_t), .rs1_val(rs1_val_t), .rs2_val(rs2_val_t), .funct3(funct3_t),
    .branchPC(branchhandler_1_branchpc));
  Adder #(.width(32)) adder_1 (.a(rs1_val_t), .b(imm_t), .out(adder_1_out));  // open: cin, cout
  Adder #(.width(32)) adder_2 (.a(currPC), .b(imm_t), .out(adder_2_out));  // open: cin, cout
  pc pc_1 (.inPC(inPC_t), .clk(clk), .outPCplus4(PCplus4), .outPC(currPC));
  Multiplexer #(.select(5), .width(32)) multiplexer_1 (
    .in0(PCplus4), .in1(PCplus4), .in2(PCplus4), .in3(PCplus4), .in4(PCplus4), .in5(PCplus4), .in6(PCplus4),
    .in7(PCplus4), .in8(PCplus4), .in9(PCplus4), .in10(PCplus4), .in11(PCplus4), .in12(PCplus4),
    .in13(PCplus4), .in14(PCplus4), .in15(PCplus4), .in16(PCplus4), .in17(PCplus4), .in18(PCplus4),
    .in19(PCplus4), .in20(PCplus4), .in21(PCplus4), .in22(PCplus4), .in23(PCplus4),
    .in24(branchhandler_1_branchpc), .in25(adder_1_out), .in26(PCplus4), .in27(adder_2_out), .in28(PCplus4),
    .in29(PCplus4), .in30(PCplus4), .in31(PCplus4), .out(inPC_t), .sel(opcode5_t));
  Register #(.width(32)) register_1 (.D(inPC_t), .en(1'b1), .clk(clk), .Q(register_1_q));  // open: clr
  ROM #(.addrWidth(19), .dataWidth(32)) myROM (.addr(register_1_q[20:2]), .data(ins_t));
  Comparator #(.width(5)) comparator_1 (.a(opcode5_t), .b(5'b01100), .eq(comparator_1_eq));  // open: gt, lt
  Comparator #(.width(5)) comparator_2 (.a(opcode5_t), .b(5'b00100), .eq(comparator_2_eq));  // open: gt, lt
  Comparator #(.width(5)) comparator_3 (.a(opcode5_t), .b({5{1'b0}}), .eq(comparator_3_eq));  // open: gt, lt
  Comparator #(.width(5)) comparator_4 (.a(opcode5_t), .b(5'b11011), .eq(comparator_4_eq));  // open: gt, lt
  Comparator #(.width(5)) comparator_5 (.a(opcode5_t), .b(5'b11001), .eq(comparator_5_eq));  // open: gt, lt
  Comparator #(.width(5)) comparator_6 (.a(opcode5_t), .b(5'b01101), .eq(comparator_6_eq));  // open: gt, lt
  Comparator #(.width(5)) comparator_7 (.a(opcode5_t), .b(5'b00101), .eq(comparator_7_eq));  // open: gt, lt
  insDecoder insdecoder_1 (
    .ins(ins_t), .opcode5(opcode5_t), .rd(rd_t), .funct3(funct3_t), .rs1(rs1_t), .rs2(rs2_t),
    .funct7(funct7_t), .imm(imm_t));
  or or_1 (or_1_out, comparator_1_eq, comparator_2_eq, comparator_3_eq, comparator_4_eq, comparator_5_eq, comparator_6_eq, comparator_7_eq);
  register_file register_file_1 (
    .rs1(rs1_t), .rs2(rs2_t), .WE(or_1_out), .rd(rd_t), .rd_val(rd_val_t), .clk(clk), .rs1_val(rs1_val_t),
    .rs2_val(rs2_val_t));
  Multiplexer #(.select(2), .width(4)) multiplexer_2 (
    .in0(4'b0001), .in1(4'b0010), .in2(4'b0100), .in3(4'b1000), .out(multiplexer_2_out), .sel(byteSel));
  Multiplexer #(.select(2), .width(4)) multiplexer_3 (
    .in0(4'b0011), .in2(4'b1100), .out(multiplexer_3_out), .sel(byteSel));  // open: in1, in3
  Multiplexer #(.select(3), .width(4)) multiplexer_4 (
    .in0(multiplexer_2_out), .in1(multiplexer_3_out), .in2(4'b1111),
    .out({byteEnable3, byteEnable2, byteEnable1, byteEnable0}), .sel(funct3_t));  // open: in3, in4, in5, in6, in7
  Multiplexer #(.select(2), .width(5)) multiplexer_5 (
    .in0({5{1'b0}}), .in1(5'b01000), .in2(5'b10000), .in3(5'b11000), .out(multiplexer_5_out), .sel(byteSel));
  Adder #(.width(32)) adder_3 (.a(rs1_val_t), .b(imm_t), .out({adder_3_out, byteSel}));  // open: cin, cout
  Comparator #(.width(5)) comparator_8 (.a(opcode5_t), .b(5'b01000), .eq(comparator_8_eq));  // open: gt, lt
  Comparator #(.width(5)) comparator_9 (.a(opcode5_t), .b({5{1'b0}}), .eq(comparator_9_eq));  // open: gt, lt
  Multiplexer #(.width(32)) multiplexer_6 (
    .in0(rs2_val_t), .in1(imm_t), .out(multiplexer_6_out), .sel(comparator_10_eq));
  Comparator #(.width(5)) comparator_10 (.a(opcode5_t), .b(5'b00100), .eq(comparator_10_eq));  // open: gt, lt
  Shifter #(.width(32)) shifter_1 (.in(rs2_val_t), .\dist (multiplexer_5_out), .out(shifter_1_out));
  RAM #(.addrWidth(24), .byteenables("byteEnables"), .dataWidth(32)) myRAM (
    .addr(adder_3_out[25:2]), .we(comparator_8_eq), .oe(comparator_9_eq), .clk(clk), .din(shifter_1_out),
    .dout(myRAM_dout), .be3(byteEnable3), .be2(byteEnable2), .be1(byteEnable1), .be0(byteEnable0));
  ALU alu_1 (
    .dataA(rs1_val_t), .dataB(multiplexer_6_out), .opcode5(opcode5_t), .funct3(funct3_t), .funct7(funct7_t),
    .data_res(ALU_res));
  assign bit_extender_1_out = {{24{myRAM_dout[7]}}, myRAM_dout[7:0]};  // Bit_Extender bit_extender_1
  assign bit_extender_2_out = {{16{myRAM_dout[15]}}, myRAM_dout[15:0]};  // Bit_Extender bit_extender_2
  assign bit_extender_3_out = {{24{1'b0}}, myRAM_dout[7:0]};  // Bit_Extender bit_extender_3
  assign bit_extender_4_out = {{16{1'b0}}, myRAM_dout[15:0]};  // Bit_Extender bit_extender_4
  Multiplexer #(.select(3), .width(32)) multiplexer_7 (
    .in0(bit_extender_1_out), .in1(bit_extender_2_out), .in2(myRAM_dout), .in4(bit_extender_3_out),
    .in5(bit_extender_4_out), .out(RAM_res), .sel(funct3_t));  // open: in3, in6, in7
  Adder #(.width(32)) adder_4 (.a(currPC), .b(imm_t), .out(adder_4_out));  // open: cin, cout
  Multiplexer #(.select(5), .width(32)) multiplexer_8 (
    .in0(RAM_res), .in1(ALU_res), .in2(ALU_res), .in3(ALU_res), .in4(ALU_res), .in5(adder_4_out),
    .in6(ALU_res), .in7(ALU_res), .in8(ALU_res), .in9(ALU_res), .in10(ALU_res), .in11(ALU_res),
    .in12(ALU_res), .in13(imm_t), .in14(ALU_res), .in15(ALU_res), .in16(ALU_res), .in17(ALU_res),
    .in18(ALU_res), .in19(ALU_res), .in20(ALU_res), .in21(ALU_res), .in22(ALU_res), .in23(ALU_res),
    .in24(ALU_res), .in25(PCplus4), .in26(ALU_res), .in27(PCplus4), .in28(ALU_res), .in29(ALU_res),
    .in30(ALU_res), .in31(ALU_res), .out(rd_val_t), .sel(opcode5_t));
endmodule

module pc (
  input  [31:0] inPC,
  input  clk,
  output [31:0] outPCplus4,
  output [31:0] outPC
);

  Register #(.width(32)) register_1 (.D(inPC), .en(1'b1), .clk(clk), .Q(outPC));  // open: clr
  Adder #(.width(32)) adder_1 (.a(outPC), .b(32'h4), .out(outPCplus4));  // open: cin, cout

  // Other names for the same wires on the sheet: clk_t = clk
endmodule

module register_file (
  input  [4:0] rs1,
  input  [4:0] rs2,
  input  WE,
  input  [4:0] rd,
  input  [31:0] rd_val,
  input  clk,
  output [31:0] rs1_val,
  output [31:0] rs2_val
);

  wire we_18, we_x0, we_x1, we_x2, we_x3, we_x4, we_x5, we_x6, we_x7, we_x8, we_x9, we_x10, we_x11, we_x12,
       we_x13, we_x14, we_x15, we_x16, we_x17, we_x18, we_x19, we_x20, we_x21, we_x22, we_x23, we_x24,
       we_x25, we_x26, we_x27, we_x28, we_x29, we_x30, we_x31;
  wire [31:0] q_x1, q_x2, q_x3, q_x4, q_x5, q_x6, q_x7, q_x8, q_x9, q_x10, q_x11, q_x12, q_x13, q_x14, q_x15,
       q_x16, q_x17, q_x18, q_x19, q_x20, q_x21, q_x22, q_x23, q_x24, q_x25, q_x26, q_x27, q_x28, q_x29,
       q_x30, q_x31;

  Demultiplexer #(.select(5)) demultiplexer_1 (
    .out0(we_x0), .out1(we_x1), .out2(we_x2), .out3(we_x3), .out4(we_x4), .out5(we_x5), .out6(we_x6),
    .out7(we_x7), .out8(we_x8), .out9(we_x9), .out10(we_x10), .out11(we_x11), .out12(we_x12), .out13(we_x13),
    .out14(we_x14), .out15(we_x15), .out16(we_x16), .out17(we_x17), .out18(we_x18), .out19(we_x19),
    .out20(we_x20), .out21(we_x21), .out22(we_x22), .out23(we_x23), .out24(we_x24), .out25(we_x25),
    .out26(we_x26), .out27(we_x27), .out28(we_x28), .out29(we_x29), .out30(we_x30), .out31(we_x31), .in(WE),
    .sel(rd));
  Register #(.width(32)) x4 (.D(rd_val), .en(we_x4), .clk(clk), .Q(q_x4));  // open: clr
  Register #(.width(32)) x8 (.D(rd_val), .en(we_x8), .clk(clk), .Q(q_x8));  // open: clr
  Register #(.width(32)) x12 (.D(rd_val), .en(we_x12), .clk(clk), .Q(q_x12));  // open: clr
  Register #(.width(32)) x16 (.D(rd_val), .en(we_x16), .clk(clk), .Q(q_x16));  // open: clr
  Register #(.width(32)) x20 (.D(rd_val), .en(we_x20), .clk(clk), .Q(q_x20));  // open: clr
  Register #(.width(32)) x24 (.D(rd_val), .en(we_x24), .clk(clk), .Q(q_x24));  // open: clr
  Register #(.width(32)) x28 (.D(rd_val), .en(we_x28), .clk(clk), .Q(q_x28));  // open: clr
  Register #(.width(32)) x1 (.D(rd_val), .en(we_x1), .clk(clk), .Q(q_x1));  // open: clr
  Register #(.width(32)) x5 (.D(rd_val), .en(we_x5), .clk(clk), .Q(q_x5));  // open: clr
  Register #(.width(32)) x9 (.D(rd_val), .en(we_x9), .clk(clk), .Q(q_x9));  // open: clr
  Register #(.width(32)) x13 (.D(rd_val), .en(we_x13), .clk(clk), .Q(q_x13));  // open: clr
  Register #(.width(32)) x17 (.D(rd_val), .en(we_x17), .clk(clk), .Q(q_x17));  // open: clr
  Register #(.width(32)) x21 (.D(rd_val), .en(we_x21), .clk(clk), .Q(q_x21));  // open: clr
  Register #(.width(32)) x25 (.D(rd_val), .en(we_x25), .clk(clk), .Q(q_x25));  // open: clr
  Register #(.width(32)) x29 (.D(rd_val), .en(we_x29), .clk(clk), .Q(q_x29));  // open: clr
  Register #(.width(32)) x2 (.D(rd_val), .en(we_x2), .clk(clk), .Q(q_x2));  // open: clr
  Register #(.width(32)) x6 (.D(rd_val), .en(we_x6), .clk(clk), .Q(q_x6));  // open: clr
  Register #(.width(32)) x10 (.D(rd_val), .en(we_x10), .clk(clk), .Q(q_x10));  // open: clr
  Register #(.width(32)) x14 (.D(rd_val), .en(we_x14), .clk(clk), .Q(q_x14));  // open: clr
  Register #(.width(32)) x18 (.D(rd_val), .en(we_18), .clk(clk), .Q(q_x18));  // open: clr
  Register #(.width(32)) x22 (.D(rd_val), .en(we_x22), .clk(clk), .Q(q_x22));  // open: clr
  Register #(.width(32)) x26 (.D(rd_val), .en(we_x26), .clk(clk), .Q(q_x26));  // open: clr
  Register #(.width(32)) x30 (.D(rd_val), .en(we_x30), .clk(clk), .Q(q_x30));  // open: clr
  Register #(.width(32)) x3 (.D(rd_val), .en(we_x3), .clk(clk), .Q(q_x3));  // open: clr
  Register #(.width(32)) x7 (.D(rd_val), .en(we_x7), .clk(clk), .Q(q_x7));  // open: clr
  Register #(.width(32)) x11 (.D(rd_val), .en(we_x11), .clk(clk), .Q(q_x11));  // open: clr
  Register #(.width(32)) x15 (.D(rd_val), .en(we_x15), .clk(clk), .Q(q_x15));  // open: clr
  Register #(.width(32)) x19 (.D(rd_val), .en(we_x19), .clk(clk), .Q(q_x19));  // open: clr
  Register #(.width(32)) x23 (.D(rd_val), .en(we_x23), .clk(clk), .Q(q_x23));  // open: clr
  Register #(.width(32)) x27 (.D(rd_val), .en(we_x27), .clk(clk), .Q(q_x27));  // open: clr
  Register #(.width(32)) x31 (.D(rd_val), .en(we_x31), .clk(clk), .Q(q_x31));  // open: clr
  Multiplexer #(.select(5), .width(32)) multiplexer_1 (
    .in0({32{1'b0}}), .in1(q_x1), .in2(q_x2), .in3(q_x3), .in4(q_x4), .in5(q_x5), .in6(q_x6), .in7(q_x7),
    .in8(q_x8), .in9(q_x9), .in10(q_x10), .in11(q_x11), .in12(q_x12), .in13(q_x13), .in14(q_x14),
    .in15(q_x15), .in16(q_x16), .in17(q_x17), .in18(q_x18), .in19(q_x19), .in20(q_x20), .in21(q_x21),
    .in22(q_x22), .in23(q_x23), .in24(q_x24), .in25(q_x25), .in26(q_x26), .in27(q_x27), .in28(q_x28),
    .in29(q_x29), .in30(q_x30), .in31(q_x31), .out(rs1_val), .sel(rs1));
  Multiplexer #(.select(5), .width(32)) multiplexer_2 (
    .in0({32{1'b0}}), .in1(q_x1), .in2(q_x2), .in3(q_x3), .in4(q_x4), .in5(q_x5), .in6(q_x6), .in7(q_x7),
    .in8(q_x8), .in9(q_x9), .in10(q_x10), .in11(q_x11), .in12(q_x12), .in13(q_x13), .in14(q_x14),
    .in15(q_x15), .in16(q_x16), .in17(q_x17), .in18(q_x18), .in19(q_x19), .in20(q_x20), .in21(q_x21),
    .in22(q_x22), .in23(q_x23), .in24(q_x24), .in25(q_x25), .in26(q_x26), .in27(q_x27), .in28(q_x28),
    .in29(q_x29), .in30(q_x30), .in31(q_x31), .out(rs2_val), .sel(rs2));

  // Other names for the same wires on the sheet: clk_t = clk; rd_val_t[31:0] = rd_val; rs1_t[4:0] = rs1;
  //   rs2_t[4:0] = rs2
endmodule

module ALU (
  input  [31:0] dataA,
  input  [31:0] dataB,
  input  [4:0] opcode5,
  input  [2:0] funct3,
  input  [6:0] funct7,
  output [31:0] data_res
);

  wire and_1_out, comparator_1_eq, comparator_2_eq, comparator_3_eq, comparator_4_lt, comparator_5_lt,
       or_1_out;
  wire [3:3] sel_t;
  wire [31:0] add_out, and_out, or_out, sll_out, slt_out, sltu_out, sra_out, srl_out, sub_out, xor_out;

  Comparator #(.width(5)) comparator_1 (.a(opcode5), .b(5'b00100), .eq(comparator_1_eq));  // open: gt, lt
  Comparator #(.width(3)) comparator_2 (.a(funct3), .b(3'b101), .eq(comparator_2_eq));  // open: gt, lt
  Comparator #(.width(5)) comparator_3 (.a(opcode5), .b(5'b01100), .eq(comparator_3_eq));  // open: gt, lt
  and and_1 (and_1_out, comparator_1_eq, comparator_2_eq);
  Multiplexer multiplexer_1 (.in0(1'b0), .in1(funct7[5]), .out(sel_t[3]), .sel(or_1_out));
  or or_1 (or_1_out, comparator_3_eq, and_1_out);
  Adder #(.width(32)) adder_1 (.a(dataA), .b(dataB), .out(add_out));  // open: cin, cout
  Shifter #(.width(32)) shifter_1 (.in(dataA), .\dist (dataB[4:0]), .out(sll_out));
  Comparator #(.width(32)) comparator_4 (.a(dataA), .b(dataB), .lt(comparator_4_lt));  // open: gt, eq
  Comparator #(.mode("unsigned"), .width(32)) comparator_5 (
    .a(dataA), .b(dataB), .lt(comparator_5_lt));  // open: gt, eq
  assign xor_out = dataA ^ dataB;  // XOR_Gate xor_1, 32 bits wide
  Shifter #(.shift("lr"), .width(32)) shifter_2 (.in(dataA), .\dist (dataB[4:0]), .out(srl_out));
  assign or_out = dataA | dataB;  // OR_Gate or_2, 32 bits wide
  assign and_out = dataA & dataB;  // AND_Gate and_2, 32 bits wide
  Subtractor #(.width(32)) subtractor_1 (.a(dataA), .b(dataB), .out(sub_out));  // open: bin, bout
  Shifter #(.shift("ar"), .width(32)) shifter_3 (.in(dataA), .\dist (dataB[4:0]), .out(sra_out));
  assign slt_out = {{31{1'b0}}, comparator_4_lt};  // Bit_Extender bit_extender_1
  assign sltu_out = {{31{1'b0}}, comparator_5_lt};  // Bit_Extender bit_extender_2
  Multiplexer #(.select(4), .width(32)) multiplexer_2 (
    .in0(add_out), .in1(sll_out), .in2(slt_out), .in3(sltu_out), .in4(xor_out), .in5(srl_out), .in6(or_out),
    .in7(and_out), .in8(sub_out), .in13(sra_out), .out(data_res), .sel({sel_t[3], funct3}));  // open: in9, in10, in11, in12, in14, in15

  // Other names for the same wires on the sheet: dataA_t[31:0] = dataA; dataB_5LSB_t[4:0] = dataB[4:0];
  //   dataB_t[31:0] = dataB; opcode5_t[4:0] = opcode5; funct3_t[2:0] = funct3; sel_t[2:0] = funct3
endmodule

module insDecoder (
  input  [31:0] ins,
  output [4:0] opcode5,
  output [4:0] rd,
  output [2:0] funct3,
  output [4:0] rs1,
  output [4:0] rs2,
  output [6:0] funct7,
  output [31:0] imm
);

  immGen immgen_1 (.ins(ins), .opcode5(ins[6:2]), .imm31_0(imm));

  assign funct3 = ins[14:12];
  assign funct7 = ins[31:25];
  assign opcode5 = ins[6:2];
  assign rd = ins[11:7];
  assign rs1 = ins[19:15];
  assign rs2 = ins[24:20];

  // Other names for the same wires on the sheet: opcode5_t[4:0] = ins[6:2]
endmodule

module branchHandler (
  input  [31:0] currPC,
  input  [31:0] imm,
  input  [31:0] rs1_val,
  input  [31:0] rs2_val,
  input  [2:0] funct3,
  output [31:0] branchPC
);

  wire branchTaken, comparator_1_gt, comparator_2_eq, comparator_2_gt, eq, ge, geu, lt, ltu, ne;
  wire [31:0] adder_1_out, adder_2_out;

  Comparator #(.width(32)) comparator_1 (.a(rs1_val), .b(rs2_val), .gt(comparator_1_gt), .eq(eq), .lt(lt));
  Comparator #(.mode("unsigned"), .width(32)) comparator_2 (
    .a(rs1_val), .b(rs2_val), .gt(comparator_2_gt), .eq(comparator_2_eq), .lt(ltu));
  or or_1 (geu, comparator_2_gt, comparator_2_eq);
  or or_2 (ge, comparator_1_gt, eq);
  not not_1 (ne, eq);
  Multiplexer #(.select(3)) multiplexer_1 (
    .in0(eq), .in1(ne), .in4(lt), .in5(ge), .in6(ltu), .in7(geu), .out(branchTaken), .sel(funct3));  // open: in2, in3
  Adder #(.width(32)) adder_1 (.a(currPC), .b(32'h4), .out(adder_1_out));  // open: cin, cout
  Adder #(.width(32)) adder_2 (.a(currPC), .b(imm), .out(adder_2_out));  // open: cin, cout
  Multiplexer #(.width(32)) multiplexer_2 (.in0(adder_1_out), .in1(adder_2_out), .out(branchPC), .sel(branchTaken));

  // Other names for the same wires on the sheet: currPC_t[31:0] = currPC; funct3_t[2:0] = funct3; imm_t[31:0] = imm;
  //   rs1_val_t[31:0] = rs1_val; rs2_val_t[31:0] = rs2_val
endmodule

module immGen (
  input  [31:0] ins,
  input  [4:0] opcode5,
  output [31:0] imm31_0
);

  wire [3:0] bsplitter_1_imm4_1;
  wire [4:0] ssplitter_1_imm4_0;
  wire [5:0] bsplitter_1_imm10_5;
  wire [6:0] ssplitter_1_imm11_5;
  wire [7:0] jsplitter_1_imm19_12;
  wire [9:0] jsplitter_1_imm10_1;
  wire [11:0] isplitter_1_imm11_0;
  wire [12:11] bsplitter_1_imm11;
  wire [20:11] jsplitter_1_imm11;
  wire [31:0] bImm, iImm, jImm, sImm;
  wire [31:12] uImm;

  iSplitter isplitter_1 (.ins(ins), .imm11_0(isplitter_1_imm11_0));  // open: opcode, rd, funct3, rs1
  sSplitter ssplitter_1 (
    .ins(ins), .imm4_0(ssplitter_1_imm4_0), .imm11_5(ssplitter_1_imm11_5));  // open: opcode, funct3, rs1, rs2
  bSplitter bsplitter_1 (
    .ins(ins), .imm11(bsplitter_1_imm11[11]), .imm4_1(bsplitter_1_imm4_1), .imm10_5(bsplitter_1_imm10_5),
    .imm12(bsplitter_1_imm11[12]));  // open: opcode, funct3, rs1, rs2
  uSplitter usplitter_1 (.ins(ins), .imm31_12(uImm));  // open: opcode, rd
  jSplitter jsplitter_1 (
    .ins(ins), .imm19_12(jsplitter_1_imm19_12), .imm11(jsplitter_1_imm11[11]), .imm10_1(jsplitter_1_imm10_1),
    .imm20(jsplitter_1_imm11[20]));  // open: opcode, rd
  assign iImm = {{20{isplitter_1_imm11_0[11]}}, isplitter_1_imm11_0};  // Bit_Extender bit_extender_1
  assign sImm = {{20{ssplitter_1_imm11_5[6]}}, {ssplitter_1_imm11_5, ssplitter_1_imm4_0}};  // Bit_Extender bit_extender_2
  assign jImm = {{11{jsplitter_1_imm11[20]}}, {jsplitter_1_imm11[20], jsplitter_1_imm19_12, jsplitter_1_imm11[11], jsplitter_1_imm10_1, 1'b0}};  // Bit_Extender bit_extender_3
  assign bImm = {{19{bsplitter_1_imm11[12]}}, {bsplitter_1_imm11, bsplitter_1_imm10_5, bsplitter_1_imm4_1, 1'b0}};  // Bit_Extender bit_extender_4
  Multiplexer #(.select(5), .width(32)) multiplexer_1 (
    .in0(iImm), .in4(iImm), .in5({uImm, {12{1'b0}}}), .in8(sImm), .in13({uImm, {12{1'b0}}}), .in24(bImm),
    .in25(iImm), .in27(jImm), .out(imm31_0), .sel(opcode5));  // open: in1, in2, in3, in6, in7, in9, in10, in11, in12, in14, in15, in16, in17, in18, in19, in20, in21, in22, in23, in26, in28, in29, in30, in31

  // Other names for the same wires on the sheet: ins_t[31:0] = ins; opcode5_t[4:0] = opcode5
endmodule

module rSplitter (
  input  [31:0] ins,
  output [6:0] opcode,
  output [4:0] rd,
  output [2:0] funct3,
  output [4:0] rs1,
  output [4:0] rs2,
  output [6:0] funct7
);


  assign funct3 = ins[14:12];
  assign funct7 = ins[31:25];
  assign opcode = ins[6:0];
  assign rd = ins[11:7];
  assign rs1 = ins[19:15];
  assign rs2 = ins[24:20];

  // Notes on the sheet:
  //   R splitter
endmodule

module iSplitter (
  input  [31:0] ins,
  output [6:0] opcode,
  output [4:0] rd,
  output [2:0] funct3,
  output [4:0] rs1,
  output [11:0] imm11_0
);


  assign funct3 = ins[14:12];
  assign imm11_0 = ins[31:20];
  assign opcode = ins[6:0];
  assign rd = ins[11:7];
  assign rs1 = ins[19:15];

  // Notes on the sheet:
  //   I splitter
endmodule

module sSplitter (
  input  [31:0] ins,
  output [6:0] opcode,
  output [4:0] imm4_0,
  output [2:0] funct3,
  output [4:0] rs1,
  output [4:0] rs2,
  output [6:0] imm11_5
);


  assign funct3 = ins[14:12];
  assign imm4_0 = ins[11:7];
  assign imm11_5 = ins[31:25];
  assign opcode = ins[6:0];
  assign rs1 = ins[19:15];
  assign rs2 = ins[24:20];

  // Notes on the sheet:
  //   S splitter
endmodule

module bSplitter (
  input  [31:0] ins,
  output [6:0] opcode,
  output imm11,
  output [3:0] imm4_1,
  output [2:0] funct3,
  output [4:0] rs1,
  output [4:0] rs2,
  output [5:0] imm10_5,
  output imm12
);


  assign funct3 = ins[14:12];
  assign imm4_1 = ins[11:8];
  assign imm10_5 = ins[30:25];
  assign imm11 = ins[7];
  assign imm12 = ins[31];
  assign opcode = ins[6:0];
  assign rs1 = ins[19:15];
  assign rs2 = ins[24:20];

  // Notes on the sheet:
  //   B splitter
endmodule

module uSplitter (
  input  [31:0] ins,
  output [6:0] opcode,
  output [4:0] rd,
  output [19:0] imm31_12
);


  assign imm31_12 = ins[31:12];
  assign opcode = ins[6:0];
  assign rd = ins[11:7];

  // Notes on the sheet:
  //   U splitter
endmodule

module jSplitter (
  input  [31:0] ins,
  output [6:0] opcode,
  output [4:0] rd,
  output [7:0] imm19_12,
  output imm11,
  output [9:0] imm10_1,
  output imm20
);


  assign imm10_1 = ins[30:21];
  assign imm11 = ins[20];
  assign imm19_12 = ins[19:12];
  assign imm20 = ins[31];
  assign opcode = ins[6:0];
  assign rd = ins[11:7];

  // Notes on the sheet:
  //   J splitter
endmodule
